# Fritzing sketch wiring (saved by Fritzing 0.9.3b)

parts:
  Raspberry_Pi_Zero1 = Raspberry Pi Zero
  DotStar1 = DorStar LED Strip [part_number=2239]
  JACK1 = 2.1mm Barrel Jack with Terminal Block

nets:
  N1: Raspberry_Pi_Zero1.GIPO10, DotStar1.DI
  N2: Raspberry_Pi_Zero1.GIPO11, DotStar1.CI
  N3: DotStar1.GND, JACK1.NEG
  N4: DotStar1.+5V, JACK1.POS

custom parts:
  DorStar LED Strip: DotStar LED strip, black, 60 LEDs/m
